# Fritzing sketch Indoor controller scheme (saved by Fritzing 0.9.3b)

parts:
  Часть1 = Arduino Uno (Rev3) - ICSP
  Часть2 = NRF24L01+ Breakout Board
  LCD1 = LCD screen  # not connected
  J1 = double row female pin header, 4 pins [form="♀ (female)"]

nets:
  N1: Часть1.A4/SDA, J1.pin3
  N2: Часть1.A5/SCL, J1.pin4
  N3: Часть1.ICSP_MOSI, Часть1.D11_PWM/MOSI, Часть2.MOSI
  N4: Часть1.D9_PWM, Часть2.CE
  N5: Часть1.D10_PWM/SS, Часть2.CS
  N6: Часть1.D12/MISO, Часть2.MISO
  N7: Часть1.D13/SCK, Часть2.SCK
  3V3: Часть1.3V3, Часть2.VCC
  N8: Часть1.5V, J1.pin2
  GND: Часть1.GND, Часть2.GND, J1.pin1

notes:
  9V Supply-------->
